# Fritzing sketch TrafficLights_V1 (saved by Fritzing 0.9.3b)
breadboards: 1

parts:
  Part1 = Arduino Mega 2560 (Rev3)
  A1 = BBAA100043  # not connected
  A2 = BBAA100043  # not connected
  A3 = BBAA100043
  A4 = BBAA100043
  A5 = BBAA100043  # not connected
  A6 = BBAA100043  # not connected
  A7 = BBAA100043  # not connected
  hc-sr1 = hc-sr04
  hc-sr2 = hc-sr04  # not connected
  hc-sr3 = hc-sr04  # not connected
  hc-sr4 = hc-sr04  # not connected
  A8 = BBAA100043
  A9 = BBAA100043  # not connected
  A10 = BBAA100043  # not connected
  A11 = BBAA100043  # not connected
  S1 = Pushbutton [package="[SMD]"]  # not connected
  S2 = Pushbutton [package="[SMD]"]  # not connected
  S3 = Momentary Switch [package=ksa_sealed_tac_switch]
  S4 = Momentary Switch [package=ksa_sealed_tac_switch]  # not connected
  S5 = Momentary Switch [package=ksa_sealed_tac_switch]  # not connected
  S6 = Momentary Switch [package=ksa_sealed_tac_switch]  # not connected
  S7 = Momentary Switch [package=ksa_sealed_tac_switch]  # not connected
  S8 = Momentary Switch [package=ksa_sealed_tac_switch]
  hc-sr5 = hc-sr04
  A12 = BBAA100043
  A13 = BBAA100043
  A14 = BBAA100043
  S9 = Momentary Switch [package=ksa_sealed_tac_switch]
  S10 = Momentary Switch [package=ksa_sealed_tac_switch]
  hc-sr6 = hc-sr04
  A15 = BBAA100043
  A16 = BBAA100043
  A17 = BBAA100043
  S11 = Momentary Switch [package=ksa_sealed_tac_switch]
  S12 = Momentary Switch [package=ksa_sealed_tac_switch]
  hc-sr7 = hc-sr04
  A18 = BBAA100043
  A19 = BBAA100043
  A20 = BBAA100043
  S13 = Momentary Switch [package=ksa_sealed_tac_switch]
  S14 = Momentary Switch [package=ksa_sealed_tac_switch]

nets:
  N1: Part1.D19/RX1, hc-sr6.Trig
  N2: Part1.D18/TX1, hc-sr6.Echo
  N3: Part1.D17_PWM/RX2, hc-sr5.Trig
  N4: Part1.D16_PWM/TX2, hc-sr5.Echo
  N5: Part1.D15/RX3, hc-sr1.Trig
  N6: Part1.D14/TX3, hc-sr1.Echo
  GND: Part1.GND, A3.pin4, A4.pin4, hc-sr1.GND, A8.pin4, S3.1, S8.1, hc-sr5.GND, A12.pin4, A13.pin4, A14.pin4, S9.1, S10.1
  N7: Part1.D11_PWM, A20.pin1
  N8: Part1.D10_PWM, A20.pin2
  N9: Part1.D9_PWM, A20.pin3
  N10: Part1.D8_PWM, A17.pin1
  N11: Part1.D0_RX0, A8.pin3, hc-sr7.Trig
  N12: Part1.D1_TX0, A8.pin2, hc-sr7.Echo
  N13: Part1.D2_PWM, A8.pin1
  N14: Part1.D3_PWM, A14.pin3
  N15: Part1.D4_PWM, A14.pin2
  N16: Part1.D5_PWM, A14.pin1
  N17: Part1.D6_PWM, A17.pin3
  N18: Part1.D7_PWM, A17.pin2
  VCC: Part1.5V, hc-sr1.VCC, hc-sr5.VCC, hc-sr6.VCC, hc-sr7.VCC
  N19: Part1.D22, A3.pin1, A4.pin1
  N20: Part1.D23, A3.pin2, A3.pin3, A4.pin3
  N21: Part1.D24, A12.pin1, A13.pin1
  N22: Part1.D25, A12.pin2, A12.pin3, A13.pin3
  N23: Part1.D26, A15.pin1, A16.pin1
  N24: Part1.D27, A15.pin2, A15.pin3, A16.pin3
  N25: Part1.D28, A18.pin1, A19.pin1
  N26: Part1.D29, A18.pin2, A18.pin3, A19.pin3
  N27: Part1.D50, S11.4, S12.4
  N28: Part1.D52, S9.4, S10.4
  N29: Part1.D53, S3.4, S8.4
  N30: hc-sr6.GND, A15.pin4, A16.pin4, A17.pin4, S11.1, S12.1
  N31: hc-sr7.GND, A18.pin4, A19.pin4, A20.pin4, S13.1, S14.1

custom parts:
  BBAA100043: BBAA100043 traffic light module.
